// Logisim project CPU.circ as structural Verilog: 6 circuits, main circuit CPU
module CPU (
);

  Clock clock_1 ();  // open: out
  PC pc_1 ();  // open: jump_addr, jump_e, clock, reset, O
endmodule

module PC (
  input  [15:0] jump_addr,
  input  jump_e,
  input  clock,
  input  reset,
  output [15:0] O
);

  wire [15:0] multiplexer_1_out, sixteenbitadder_1_o;

  sixteenbitadder sixteenbitadder_1 (.Cin(1'b1), .A(O), .O(sixteenbitadder_1_o));  // open: B, Cout
  Multiplexer #(.width(16)) multiplexer_1 (
    .in0(sixteenbitadder_1_o), .in1(jump_addr), .out(multiplexer_1_out), .sel(jump_e));
  Register #(.width(16)) register_1 (.D(multiplexer_1_out), .en(1'b1), .clk(clock), .Q(O), .clr(reset));
endmodule

module sixteenbitadder (
  input  Cin,
  input  [15:0] A,
  input  [15:0] B,
  output [15:0] O,
  output Cout
);

  wire fourbitadder_1_cout, fourbitadder_2_cout, fourbitadder_3_cout;

  fourbitadder fourbitadder_1 (.Cin(Cin), .A(A[3:0]), .B(B[3:0]), .O(O[3:0]), .Cout(fourbitadder_1_cout));
  fourbitadder fourbitadder_2 (
    .Cin(fourbitadder_1_cout), .A(A[7:4]), .B(B[7:4]), .O(O[7:4]), .Cout(fourbitadder_2_cout));
  fourbitadder fourbitadder_3 (
    .Cin(fourbitadder_2_cout), .A(A[11:8]), .B(B[11:8]), .O(O[11:8]), .Cout(fourbitadder_3_cout));
  fourbitadder fourbitadder_4 (.Cin(fourbitadder_3_cout), .A(A[15:12]), .B(B[15:12]), .O(O[15:12]), .Cout(Cout));
endmodule

module fourbitadder (
  input  Cin,
  input  [3:0] A,
  input  [3:0] B,
  output [3:0] O,
  output Cout
);

  wire fulladder_1_cout, fulladder_2_cout, fulladder_3_cout;

  fulladder fulladder_1 (.Cin(Cin), .A(A[0]), .B(B[0]), .O(O[0]), .Cout(fulladder_1_cout));
  fulladder fulladder_2 (.Cin(fulladder_1_cout), .A(A[1]), .B(B[1]), .O(O[1]), .Cout(fulladder_2_cout));
  fulladder fulladder_3 (.Cin(fulladder_2_cout), .A(A[2]), .B(B[2]), .O(O[2]), .Cout(fulladder_3_cout));
  fulladder fulladder_4 (.Cin(fulladder_3_cout), .A(A[3]), .B(B[3]), .O(O[3]), .Cout(Cout));
endmodule

module halfadder (
  input  A,
  input  B,
  output O,
  output Cout
);

  xor xor_1 (O, A, B);
  and and_1 (Cout, A, B);
endmodule

module fulladder (
  input  Cin,
  input  A,
  input  B,
  output O,
  output Cout
);

  wire halfadder_1_cout, halfadder_2_cout, halfadder_2_o;

  halfadder halfadder_1 (.A(Cin), .B(halfadder_2_o), .O(O), .Cout(halfadder_1_cout));
  halfadder halfadder_2 (.A(A), .B(B), .O(halfadder_2_o), .Cout(halfadder_2_cout));
  or or_1 (Cout, halfadder_1_cout, halfadder_2_cout);
endmodule
